# Fritzing sketch lcd_keypad (saved by Fritzing 0.9.4)
breadboards: 1

parts:
  U1 = LCD-16X2 [package=lcd-16x2]
  Part1 = Arduino Nano (Rev3.0) (ICSP)
  R1 = TRIMPOT [package=3386u]
  R2 = Resistor [tolerance=±5% resistance=220 package="1206 [SMD]"]

nets:
  VSS: U1.VSS, Part1.GND
  VDD: U1.VDD, Part1.5V
  N1: U1.VO, R1.WIPER
  N2: U1.RS, Part1.D12/MISO
  N3: U1.R_W, U1.K, R1.CCW
  N4: U1.E, Part1.D11/MOSI
  N5: U1.DB4, Part1.D5
  N6: U1.DB5, Part1.D4
  N7: U1.DB6, Part1.D3
  N8: U1.DB7, Part1.D2
  N9: U1.A, R2.Pin_1
  N10: R1.CW, R2.Pin_0

notes:
  PWR SDA SCL GND
  for Qwiic Keypad
